# Fritzing sketch Capstone_0612 (saved by Fritzing 0.9.3b)
breadboards: 1

parts:
  부품1 = Arduino Uno (Rev3)
  U1 = Sharp Dust Sensor [part_number=GP2Y1010AU0F]
  Mod1 = YL-83 Rain Sensor - Detection Board
  Mod2 = YL-83 Rain Sensor - Control Board
  부품2 = Bluetooth HC-06
  R1 = Resistor [tolerance=±5% resistance=330 package=THT]
  R2 = Resistor [tolerance=±5% resistance=330 package=THT]
  R3 = Resistor [tolerance=±5% resistance=330 package=THT]
  R4 = Resistor [tolerance=±5% resistance=150 package=THT]
  C1 = Electrolytic Capacitor [capacitance=220nF voltage=10V package="100 mil [THT, electrolytic]"]
  Driver1 = 28BYJ-48 Driver Module [part_number=ULN2003 package=THT]
  SM1 = 28BYJ-48 Stepper Motor [part_number=28BYJ-48]

nets:
  N1: 부품1.A5/SCL, U1.Vo
  N2: 부품1.D8, Driver1.IN4
  GND: 부품1.GND, U1.S-GND, Mod2.GND, 부품2.GND, R3.Pin_0, Driver1.GND
  N3: 부품1.D2, 부품2.TXD
  N4: 부품1.D3_PWM, R1.Pin_1, R2.Pin_0
  N5: 부품1.D4, U1.LED
  N6: 부품1.D5_PWM, Driver1.IN1
  N7: 부품1.D6_PWM, Driver1.IN2
  N8: 부품1.D7, Driver1.IN3
  VCC: 부품1.5V, U1.VCC, Mod2.VCC, 부품2.VCC, R4.Pin_0, Driver1.Vmotor
  N9: U1.V-LED, C1.-
  N10: U1.LED-GND, C1.+
  N11: Mod1.POS, Mod2.POS
  N12: Mod1.NEG, Mod2.NEG
  N13: 부품2.RXD, R1.Pin_0
  N14: R2.Pin_1, R3.Pin_1
  N15: Driver1.blue-pin, SM1.blue-pin
  N16: Driver1.pink-pin, SM1.pink-pin
  N17: Driver1.yellow-pin, SM1.yellow-pin
  N18: Driver1.orange-pin, SM1.orange-pin
  N19: Driver1.red-pin, SM1.red-pin

custom parts:
  Sharp Dust Sensor: Sharp GP2Y1010AU0F Dust Sensor
  YL-83 Rain Sensor - Detection Board: The YL-83 is a rain sensor that has more resistance when dry and less resistance when wet. The module runs at 5V.
  YL-83 Rain Sensor - Control Board: The YL-83 is a rain sensor that has more resistance when dry and less resistance when wet. The module runs at 5V.
  28BYJ-48 Driver Module: ULN2003 Driver Module for the 28BYJ-48 Unipolar Stepper Motor LED A - Blue wire - Bottom coil left LED B - Pink wire - Top coil left LED C - Yellow wire - Bottom coil right LED D - Orange wire - Top coil right Common rail - red Connector pins: blue - pink - yellow - orange - red Control pins - IN1 to IN4 Power pins - GND & Vmotor (5-12V) On/Off jumper (if removed, power to motor is cut).
  28BYJ-48 Stepper Motor: Unipolar Stepper Motor 28BYJ-48 Top coil - pink & orange Bottom coil - blue & yellow Common rail - red Connector pins: blue - pink - yellow - orange - red
